// Digital circuit ContMod5Verilog.dig as structural Verilog
module ContMod5Verilog (
  input  clk,
  input  in_2
);

  wire [2:0] u_ContMod5_q;

  ContMod5 #(.applicationType("IVERILOG")) u_ContMod5 (.clk(clk), .u(in_2), .q(u_ContMod5_q));
  Seven_Seg_Hex seven_seg_hex_1 (.d({1'b0, u_ContMod5_q}), .dp(1'b0));
endmodule

/* Code of ContMod5:
module ContMod5(input clk, u, output reg [2:0] q);
 always @(negedge clk)
  begin
  if (u)
   case (q)
    0: q = 2;
    1: q = 3;
    2: q = 4;
    3: q = 0;
    4: q = 1;
    default: q = 0;
   endcase
  else
    case (q)
     0: q = 4;
     1: q = 0;
     2: q = 1;
     3: q = 2;
     4: q = 3;
     default: q = 0;
     endcase
  end
endmodule
*/
