// Digital circuit Corrigir Contador Síncrono  Mod9 - Vinicius Albuquerque.dig as structural Verilog
module \Corrigir_Contador_Síncrono__Mod9___Vinicius_Albuquerque  (
  input  Clk,
  input  Rst,
  output Q3,
  output Q2,
  output Q1,
  output Q0
);

  wire and_1_out, and_2_out, and_3_out, nand_1_out;

  Seven_Seg_Hex seven_seg_hex_1 (.d({Q3, Q2, Q1, Q0}), .dp(1'b0));
  nand nand_1 (nand_1_out, Q3, Q0);
  and and_1 (and_1_out, Rst, nand_1_out);
  JK_FF_AS jk_ff_as_1 (.Set(~1'b1), .J(1'b1), .C(~Clk), .K(1'b1), .Clr(~and_1_out), .Q(Q0));  // open: nQ
  JK_FF_AS jk_ff_as_2 (.Set(~1'b1), .J(Q0), .C(~Clk), .K(Q0), .Clr(~and_1_out), .Q(Q1));  // open: nQ
  and and_2 (and_2_out, Q0, Q1);
  JK_FF_AS jk_ff_as_3 (.Set(~1'b1), .J(and_2_out), .C(~Clk), .K(and_2_out), .Clr(~and_1_out), .Q(Q2));  // open: nQ
  and and_3 (and_3_out, Q0, Q1, Q2);
  JK_FF_AS jk_ff_as_4 (.Set(~1'b1), .J(and_3_out), .C(~Clk), .K(and_3_out), .Clr(~and_1_out), .Q(Q3));  // open: nQ
endmodule

/* Test case CntMod9:
Clk Rst Q3 Q2 Q1 Q0
0 0 bits(4,0) 
repeat(8) C 1 bits(4,n+1)
c 0 bits(4,0)
repeat(8) C 1 bits(4,n+1)
c 1 bits(4,0)
repeat(8) C 1 bits(4,n+1)
*/
