// Digital circuit Pand.dig as structural Verilog
module Pand (
  input  [3:0] in_2,
  input  [3:0] in_3,
  input  [2:0] in_4,
  output [7:0] out_1
);

  PAND #(.applicationType("IVERILOG")) u_PAND (.a(in_2), .b(in_3), .sel(in_4), .y(out_1));
endmodule

/* Code of PAND:
module PAND(input [3:0] a,b, input [2:0] sel, output reg [7:0] y);
 always @(*)
  begin
   case (sel)
    0: y = a+b;
    1: y = a-b;
    2: y = a*b;
    3: y = a/b;
    4: y = a&b;
    5: y = a^b;
    default: y=0;
   endcase
  end
endmodule
*/
