// Digital circuit TabelaVerdade3.dig as structural Verilog
module TabelaVerdade3 (
  input  C,
  input  B,
  input  A,
  input  D,
  output Z
);

  xx #(.applicationType("IVERILOG")) u_xx (.a(A), .b(B), .c(C), .d(D), .z(Z));

  // Notes on the sheet:
  //   C: default 1
  //   D: default 1
endmodule

/* Test case TabelaVerdade3:
#AUTOMATO 01010 CREP INTC
D C B A Z
bits(4,0) 0 
bits(4,1) 0 
bits(4,2) 0 
bits(4,3) 1 
bits(4,4) 0 
bits(4,5) 0 
bits(4,6) 0 
bits(4,7) 1 
bits(4,8) 0 
bits(4,9) 0 
bits(4,10) 0 
bits(4,11) 1 
bits(4,12) 1 
bits(4,13) 1 
bits(4,14) 1 
bits(4,15) 1

 
*/

/* Code of xx:
module xx(input a,input b, input c, input d, output reg z);
 always @(a,b,c,d)
   begin
   case ({d,c,b,a})
    4'b0011: z = 1'b1;
    4'b0111: z = 1'b1;
    4'b1011: z = 1'b1;
    4'b1100: z = 1'b1;
    4'b1101: z = 1'b1;
    4'b1110: z = 1'b1;
    4'b1111: z = 1'b1;
    default: z = 1'b0;
   endcase
   end
endmodule
*/
