// Digital circuit Template  Questão 7.dig as structural Verilog
module \Template__Questão_7  (
  input  B3,
  input  B2,
  input  B1,
  input  B0,
  output S3,
  output S2,
  output S1,
  output S0,
  output S4
);

  Seven_Seg_Hex seven_seg_hex_1 (.d({B3, B2, B1, B0}), .dp(1'b0));
  xx #(.applicationType("IVERILOG")) u_xx (.b0(B0), .b1(B1), .b2(B2), .b3(B3), .s({S4, S3, S2, S1, S0}));
endmodule

/* Test case PadrãoJonhson:
B3 B2 B1 B0  S4 S3 S2 S1 S0
0 0 0 0 	0 0 0 0 0
0 0 0 1 	0 0 0 0 1
0 0 1 0 	0 0 0 1 1
0 0 1 1 	0 0 1 1 1
0 1 0 0 	0 1 1 1 1
0 1 0 1 	1 1 1 1 1
0 1 1 0 	1 1 1 1 0 
0 1 1 1 	1 1 1 0 0
1 0 0 0 	1 1 0 0 0
1 0 0 1 	1 0 0 0 0
*/

/* Code of xx:
module xx(input b0,b1,b2,b3, output  reg[4:0] s);
 always @(*)
   begin
   case ({b3,b2,b1,b0})
    4'b0000: s = 5'b00000;
    4'b0001: s = 5'b00001;
    4'b0010: s = 5'b00011;
    4'b0011: s = 5'b00111;
    4'b0100: s = 5'b01111;
    4'b0101: s = 5'b11111;
    4'b0110: s = 5'b11110;
    4'b0111: s = 5'b11100;
    4'b1000: s = 5'b11000;
    4'b1001: s = 5'b10000;
    default: s = 5'b00000;
   endcase
   end
endmodule
*/
