// Digital circuit Template Contador Mod6 u3 d1 - Vinicius Albuquerque.dig as structural Verilog
module Template_Contador_Mod6_u3_d1___Vinicius_Albuquerque (
  input  U,
  input  Clk,
  output Q0,
  output Q1,
  output Q2
);

  wire nU, reset_1_out;

  Seven_Seg_Hex seven_seg_hex_1 (.d({1'b0, Q2, Q1, Q0}), .dp(1'b0));
  not not_1 (nU, U);
  ContMod5 #(.applicationType("IVERILOG")) u_ContMod5 (.clk(Clk), .u(U), .rst(reset_1_out), .q({Q2, Q1, Q0}));
  Reset reset_1 (.out(reset_1_out));

  // Notes on the sheet:
  //   U: default 1
endmodule

/* Test case MOD6 U3 D1:
#MOD6 u3 d1
Clk U Q2 Q1 Q0
C 1 bits(3,3)
C 1 bits(3,6)
C 1 bits(3,2)
C 0 bits(3,5)
C 1 bits(3,1)
C 1 bits(3,4)
C 1 bits(3,0)
C 0 bits(3,6)
C 0 bits(3,5)
C 0 bits(3,4)
C 0 bits(3,3)
C 0 bits(3,2)
C 0 bits(3,1)
C 0 bits(3,0)
*/

/* Code of ContMod5:
module ContMod5(input clk, u, rst, output reg [2:0] q);
 always @(negedge clk)
  begin
  if (~rst)
   q = 0;
  else
  if (u)
   case (q)
    0: q = 3;
    1: q = 4;
    2: q = 5;
    3: q = 6;
    4: q = 0;
    5: q = 1;
    6: q = 2;  
    default: q = 0;
   endcase
  else
    case (q)
     0: q = 6;
     1: q = 0;
     2: q = 1;
     3: q = 2;
     4: q = 3;
     5: q = 4;
     6: q = 5; 
     default: q = 0;
     endcase
  end
endmodule
*/
