// Digital circuit Template Contador Mod6 u3 d1.dig as structural Verilog
module Template_Contador_Mod6_u3_d1 (
  input  U,
  input  Clk,
  output Q0,
  output Q1,
  output Q2
);

  wire and_1_out, and_2_out, and_3_out, and_4_out, and_5_out, and_6_out, and_7_out, and_8_out, and_9_out,
       and_10_out, D0, D1, D2, nQ0, nQ1, nQ2, nU, or_2_out, or_4_out, reset_1_out, xor_1_out, xor_2_out,
       xor_3_out;

  Seven_Seg_Hex seven_seg_hex_1 (.d({1'b0, Q2, Q1, Q0}), .dp(1'b0));
  not not_1 (nU, U);
  xor xor_1 (xor_1_out, U, Q2);
  xor xor_2 (xor_2_out, U, Q2);
  and and_1 (and_1_out, xor_2_out, Q0);
  D_FF D_2 (.D(D2), .C(Clk), .Q(Q2), .nQ(nQ2));
  and and_2 (and_2_out, ~U, ~Q0, ~Q1, ~Q2);  // And
  and and_3 (and_3_out, xor_1_out, Q1);
  or or_1 (D2, and_2_out, and_3_out, and_1_out);
  or or_2 (or_2_out, ~U, ~Q2);  // Or
  and and_4 (and_4_out, ~Q1, ~Q0);  // And
  D_FF D_1 (.D(D1), .C(Clk), .Q(Q1), .nQ(nQ1));
  and and_5 (and_5_out, or_2_out, and_4_out);
  and and_6 (and_6_out, Q1, Q0);
  and and_7 (and_7_out, U, Q2, Q1);
  or or_3 (D1, and_5_out, and_6_out, and_7_out);
  Reset reset_1 (.out(reset_1_out));
  D_FF D_0 (.D(D0), .C(Clk), .Q(Q0), .nQ(nQ0));
  xor xor_3 (xor_3_out, U, Q2);
  and and_8 (and_8_out, ~Q2, Q1);  // And
  or or_4 (or_4_out, xor_3_out, and_8_out);
  and and_9 (and_9_out, or_4_out, ~Q0);  // And
  and and_10 (and_10_out, U, Q2, Q0);
  or or_5 (D0, and_9_out, and_10_out);

  // Notes on the sheet:
  //   U: default 1
endmodule

/* Test case MOD6 U3 D1:
#MOD6 u3 d1
Clk U Q2 Q1 Q0
C 1 bits(3,3)
C 1 bits(3,6)
C 1 bits(3,2)
C 0 bits(3,5)
C 1 bits(3,1)
C 1 bits(3,4)
C 1 bits(3,0)
C 0 bits(3,6)
C 0 bits(3,5)
C 0 bits(3,4)
C 0 bits(3,3)
C 0 bits(3,2)
C 0 bits(3,1)
C 0 bits(3,0)
*/
