// Digital circuit Template contador 0123401234 - Vinicius Albuquerque.dig as structural Verilog
module Template_contador_0123401234___Vinicius_Albuquerque (
  input  Clk,
  output Q0,
  output Q1,
  output Q2
);

  wire and_1_out, not_1_out, rst, TC;

  Seven_Seg_Hex seven_seg_hex_1 (.d({1'b0, Q2, Q1, Q0}), .dp(1'b0));
  and and_1 (and_1_out, Q1, Q0);
  JK_FF_AS T_c (.Set(~1'b1), .J(TC), .C(~Clk), .K(TC), .Clr(~rst), .Q(Q2));  // open: nQ
  or or_1 (TC, and_1_out, Q2);
  JK_FF_AS T_b (.Set(~1'b1), .J(Q0), .C(~Clk), .K(Q0), .Clr(~rst), .Q(Q1));  // open: nQ
  not not_1 (not_1_out, Q2);
  JK_FF_AS T_a (.Set(~1'b1), .J(not_1_out), .C(~Clk), .K(not_1_out), .Clr(~rst), .Q(Q0));  // open: nQ
  Reset reset_1 (.out(rst));
endmodule

/* Test case Contador 0123401234:
Clk Q2 Q1 Q0
C bits(3,1)
C bits(3,2)
C bits(3,3)
C bits(3,4)
C bits(3,0)
C bits(3,1)
C bits(3,2)
C bits(3,3)
C bits(3,4)
C bits(3,0)
*/
