// Digital circuit TemplateComunicacaoBCDSimples.dig as structural Verilog
module TemplateComunicacaoBCDSimples (
  input  B0,
  input  B1,
  input  B2,
  input  B3,
  input  B4,
  input  B5,
  input  B6,
  input  B7,
  input  B8,
  input  B9,
  input  B10,
  input  B11,
  input  BP,
  output ERRO
);

  xx #(.applicationType("IVERILOG")) u_xx (
    .BP(BP), .B11(B11), .B10(B10), .B9(B9), .B8(B8), .B7(B7), .B6(B6), .B5(B5), .B4(B4), .B3(B3), .B2(B2),
    .B1(B1), .B0(B0), .s(ERRO));
endmodule

/* Test case ComunicacaoBCDSimples:
B11 B10 B9 B8 B7 B6 B5 B4 B3 B2 B1 B0 BP ERRO
bits(4,1) bits(4,2) bits(4,3) 1 0
bits(4,1) bits(4,2) bits(4,3) 0 1
bits(4,5) bits(4,5) bits(4,1) 0 0
bits(4,5) bits(4,5) bits(4,1) 1 1
bits(4,7) bits(4,5) bits(4,2) 1 0
bits(4,7) bits(4,5) bits(4,2) 0 1

bits(4,9) bits(4,4) bits(4,7) 1 0
bits(4,7) bits(4,2) bits(4,3) 1 0
bits(4,3) bits(4,1) bits(4,6) 0 0
bits(4,4) bits(4,3) bits(4,3) 0 0

bits(4,9) bits(4,4) bits(4,7) 0 1
bits(4,7) bits(4,2) bits(4,3) 0 1
bits(4,3) bits(4,1) bits(4,6) 1 1
bits(4,4) bits(4,3) bits(4,3) 1 1
*/

/* Code of xx:
module xx(input BP,B11,B10,B9,B8,B7,B6,B5,B4,B3,B2,B1,B0, output s);
 assign s = ~(BP^B11^B10^B9^B8^B7^B6^B5^B4^B3^B2^B1^B0);
endmodule
*/
