// Digital circuit assincrono.dig as structural Verilog
module assincrono (
  input  in_1,
  input  clk,
  input  Clr,
  input  Set,
  output Q_0,
  output Q_1,
  output Q_2,
  output Q_3
);

  JK_FF_AS jk_ff_as_1 (.Set(Set), .J(in_1), .C(~clk), .K(in_1), .Clr(Clr), .Q(Q_0));  // open: nQ
  JK_FF_AS jk_ff_as_2 (.Set(Set), .J(in_1), .C(~Q_0), .K(in_1), .Clr(Clr), .Q(Q_1));  // open: nQ
  JK_FF_AS jk_ff_as_3 (.Set(Set), .J(in_1), .C(~Q_1), .K(in_1), .Clr(Clr), .Q(Q_2));  // open: nQ
  JK_FF_AS jk_ff_as_4 (.Set(Set), .J(in_1), .C(~Q_2), .K(in_1), .Clr(Clr), .Q(Q_3));  // open: nQ
  Seven_Seg_Hex seven_seg_hex_1 (.d({Q_3, Q_2, Q_1, Q_0}), .dp(1'b0));
endmodule
