// Digital circuit assincrono2.dig as structural Verilog
module assincrono2 (
  input  clk
);

  wire A, B, C, C_e, C_lr, D, D_e;

  JK_FF_AS jk_ff_as_1 (.Set(~1'b1), .J(1'b1), .C(~clk), .K(1'b1), .Clr(~C_lr), .Q(A));  // open: nQ
  and and_1 (C_e, A, B);
  JK_FF_AS jk_ff_as_2 (.Set(~1'b1), .J(A), .C(~clk), .K(A), .Clr(~C_lr), .Q(B));  // open: nQ
  nand nand_1 (C_lr, B, D);
  JK_FF_AS jk_ff_as_3 (.Set(~1'b1), .J(C_e), .C(~clk), .K(C_e), .Clr(~C_lr), .Q(C));  // open: nQ
  and and_2 (D_e, C_e, C);
  JK_FF_AS jk_ff_as_4 (.Set(~1'b1), .J(D_e), .C(~clk), .K(D_e), .Clr(~C_lr), .Q(D));  // open: nQ
  Seven_Seg_Hex seven_seg_hex_1 (.d({D, C, B, A}), .dp(1'b0));

  // Other names for the same wires on the sheet: Cl = clk
endmodule
