// Digital circuit contadormod5comautorecuperação.dig as structural Verilog
module \contadormod5comautorecuperação  (
  input  clk
);

  wire A, B, C, Da, Db, Dc;

  D_FF #(.Default(1)) D_C (.D(Dc), .C(clk), .Q(C));  // open: nQ
  and and_1 (Dc, ~C, B, A);  // And
  D_FF #(.Default(1)) D_B (.D(Db), .C(clk), .Q(B));  // open: nQ
  xor xor_1 (Db, A, B);
  xnor xnor_1 (Da, A, C);
  D_FF D_A (.D(Da), .C(clk), .Q(A));  // open: nQ
  Seven_Seg_Hex seven_seg_hex_1 (.d({1'b0, C, B, A}), .dp(1'b0));
endmodule
