// Digital circuit sequencial contador.dig as structural Verilog
module sequencial_contador (
  input  E_1,
  input  C_1,
  output S_0,
  output S_1,
  output S_2,
  output S_3
);

  T_FF t_ff_1 (.T(E_1), .C(~C_1), .Q(S_0));  // open: nQ
  T_FF t_ff_2 (.T(E_1), .C(~S_0), .Q(S_1));  // open: nQ
  T_FF t_ff_3 (.T(E_1), .C(~S_1), .Q(S_2));  // open: nQ
  T_FF t_ff_4 (.T(E_1), .C(~S_2), .Q(S_3));  // open: nQ
  Seven_Seg_Hex seven_seg_hex_1 (.d({S_3, S_2, S_1, S_0}), .dp(1'b0));
endmodule
