// Digital circuit u.dig as structural Verilog
module u (
  input  clk,
  input  in_2
);

  wire Q_0, Q_1, T1;

  T_FF T_1 (.T(T1), .C(clk), .Q(Q_1));  // open: nQ
  xnor xnor_1 (T1, in_2, Q_0);
  T_FF T_0 (.T(1'b1), .C(clk), .Q(Q_0));  // open: nQ
  Seven_Seg_Hex seven_seg_hex_1 (.d({2'b00, Q_1, Q_0}), .dp(1'b0));

  // Other names for the same wires on the sheet: U = in_2
endmodule
